// Digital circuit ALU.dig as structural Verilog
module ALU (
  input  [31:0] A,
  input  [31:0] B,
  input  [2:0] Sel__Op,
  output [31:0] C,
  output Zero
);

  wire [31:0] and_1_out, barrelshifter_1_out, barrelshifter_2_out, cs_cla_32bit_adder_1_s,
       cs_cla_32bit_adder_2_s, invertesinal_1_out, invertesinal_2_out, or_1_out, xor_1_out;

  inverteSinal invertesinal_1 (.In(B), .Out(invertesinal_1_out));
  CS_CLA_32bit_adder cs_cla_32bit_adder_1 (.A(A), .B(B), .S(cs_cla_32bit_adder_1_s));
  CS_CLA_32bit_adder cs_cla_32bit_adder_2 (.A(A), .B(invertesinal_1_out), .S(cs_cla_32bit_adder_2_s));
  assign and_1_out = A & B;  // And and_1, 32 bits wide
  assign or_1_out = A | B;  // Or or_1, 32 bits wide
  assign xor_1_out = A ^ B;  // XOr xor_1, 32 bits wide
  inverteSinal invertesinal_2 (.In(A), .Out(invertesinal_2_out));
  BarrelShifter #(.Bits(32)) barrelshifter_1 (.in(A), .shift(B[5:0]), .out(barrelshifter_1_out));
  BarrelShifter #(.Bits(32), .direction("right")) barrelshifter_2 (.in(A), .shift(B[5:0]), .out(barrelshifter_2_out));
  Multiplexer #(.Selector_Bits(3), .Bits(32)) multiplexer_1 (
    .sel(Sel__Op), .in_0(cs_cla_32bit_adder_1_s), .in_1(cs_cla_32bit_adder_2_s), .in_2(and_1_out),
    .in_3(or_1_out), .in_4(xor_1_out), .in_5(invertesinal_2_out), .in_6(barrelshifter_1_out),
    .in_7(barrelshifter_2_out), .out(C));
  zero zero_1 (.A(C), .Zero(Zero));
endmodule
