// Digital circuit CLA-4bit-half.dig as structural Verilog
module CLA_4bit_half (
  input  A0,
  input  B0,
  input  A1,
  input  B1,
  input  A2,
  input  B2,
  input  A3,
  input  B3,
  output S0,
  output S1,
  output S2,
  output S3,
  output C3
);

  wire and_1_out, and_2_out, and_3_out, and_4_out, and_5_out, and_6_out, and_7_out, and_8_out, and_9_out,
       and_10_out, or_1_out, or_2_out, or_3_out, or_4_out, or_6_out, or_7_out, xor_1_out, xor_2_out,
       xor_3_out;

  or or_1 (or_1_out, A3, B3);
  and and_1 (and_1_out, A3, B3);
  or or_2 (or_2_out, A2, B2);
  and and_2 (and_2_out, A2, B2);
  or or_3 (or_3_out, A1, B1);
  and and_3 (and_3_out, A1, B1);
  or or_4 (or_4_out, A0, B0);
  and and_4 (and_4_out, A0, B0);
  and and_5 (and_5_out, and_4_out, or_1_out, or_2_out, or_3_out);
  and and_6 (and_6_out, and_3_out, or_2_out, or_1_out);
  and and_7 (and_7_out, or_1_out, and_2_out);
  xor xor_1 (xor_1_out, or_1_out, and_1_out);
  and and_8 (and_8_out, or_3_out, or_2_out, and_4_out);
  and and_9 (and_9_out, or_2_out, and_3_out);
  xor xor_2 (xor_2_out, or_2_out, and_2_out);
  and and_10 (and_10_out, or_3_out, and_4_out);
  xor xor_3 (xor_3_out, or_3_out, and_3_out);
  xor xor_4 (S0, or_4_out, and_4_out);
  or or_5 (C3, and_5_out, and_6_out, and_7_out, and_1_out);
  or or_6 (or_6_out, and_8_out, and_9_out, and_2_out);
  or or_7 (or_7_out, and_10_out, and_3_out);
  xor xor_5 (S3, xor_1_out, or_6_out);
  xor xor_6 (S2, xor_2_out, or_7_out);
  xor xor_7 (S1, xor_3_out, and_4_out);

  // Notes on the sheet:
  //   A0: default 1
  //   B1: default 1
  //   B2: default 1
  //   A3: default 1
endmodule
