// Digital circuit CS-CLA-32bit-adder.dig as structural Verilog
module CS_CLA_32bit_adder (
  input  [31:0] A,
  input  [31:0] B,
  output [31:0] S
);

  wire cla_4bit_half_1_c3, cs_cla_4bit_adder_2_co, cs_cla_4bit_adder_3_co, cs_cla_4bit_adder_4_co,
       cs_cla_4bit_adder_5_co, cs_cla_4bit_adder_6_co, cs_cla_4bit_adder_7_co;

  CS_CLA_4bit_adder cs_cla_4bit_adder_1 (
    .Ci(cs_cla_4bit_adder_2_co), .a0(A[28]), .b0(B[28]), .a1(A[29]), .b1(B[29]), .a2(A[30]), .b2(B[30]),
    .a3(A[31]), .b3(B[31]), .s0(S[28]), .s1(S[29]), .s2(S[30]), .s3(S[31]));  // open: Co
  CS_CLA_4bit_adder cs_cla_4bit_adder_2 (
    .Ci(cs_cla_4bit_adder_3_co), .a0(A[24]), .b0(B[24]), .a1(A[25]), .b1(B[25]), .a2(A[26]), .b2(B[26]),
    .a3(A[27]), .b3(B[27]), .s0(S[24]), .s1(S[25]), .s2(S[26]), .s3(S[27]), .Co(cs_cla_4bit_adder_2_co));
  CS_CLA_4bit_adder cs_cla_4bit_adder_3 (
    .Ci(cs_cla_4bit_adder_4_co), .a0(A[20]), .b0(B[20]), .a1(A[21]), .b1(B[21]), .a2(A[22]), .b2(B[22]),
    .a3(A[23]), .b3(B[23]), .s0(S[20]), .s1(S[21]), .s2(S[22]), .s3(S[23]), .Co(cs_cla_4bit_adder_3_co));
  CS_CLA_4bit_adder cs_cla_4bit_adder_4 (
    .Ci(cs_cla_4bit_adder_5_co), .a0(A[16]), .b0(B[16]), .a1(A[17]), .b1(B[17]), .a2(A[18]), .b2(B[18]),
    .a3(A[19]), .b3(B[19]), .s0(S[16]), .s1(S[17]), .s2(S[18]), .s3(S[19]), .Co(cs_cla_4bit_adder_4_co));
  CS_CLA_4bit_adder cs_cla_4bit_adder_5 (
    .Ci(cs_cla_4bit_adder_6_co), .a0(A[12]), .b0(B[12]), .a1(A[13]), .b1(B[13]), .a2(A[14]), .b2(B[14]),
    .a3(A[15]), .b3(B[15]), .s0(S[12]), .s1(S[13]), .s2(S[14]), .s3(S[15]), .Co(cs_cla_4bit_adder_5_co));
  CS_CLA_4bit_adder cs_cla_4bit_adder_6 (
    .Ci(cs_cla_4bit_adder_7_co), .a0(A[8]), .b0(B[8]), .a1(A[9]), .b1(B[9]), .a2(A[10]), .b2(B[10]),
    .a3(A[11]), .b3(B[11]), .s0(S[8]), .s1(S[9]), .s2(S[10]), .s3(S[11]), .Co(cs_cla_4bit_adder_6_co));
  CS_CLA_4bit_adder cs_cla_4bit_adder_7 (
    .Ci(cla_4bit_half_1_c3), .a0(A[4]), .b0(B[4]), .a1(A[5]), .b1(B[5]), .a2(A[6]), .b2(B[6]), .a3(A[7]),
    .b3(B[7]), .s0(S[4]), .s1(S[5]), .s2(S[6]), .s3(S[7]), .Co(cs_cla_4bit_adder_7_co));
  CLA_4bit_half cla_4bit_half_1 (
    .A0(A[0]), .B0(B[0]), .A1(A[1]), .B1(B[1]), .A2(A[2]), .B2(B[2]), .A3(A[3]), .B3(B[3]), .S0(S[0]),
    .S1(S[1]), .S2(S[2]), .S3(S[3]), .C3(cla_4bit_half_1_c3));
endmodule
