// Digital circuit CS-CLA-4bit-adder.dig as structural Verilog
module CS_CLA_4bit_adder (
  input  Ci,
  input  a0,
  input  b0,
  input  a1,
  input  b1,
  input  a2,
  input  b2,
  input  a3,
  input  b3,
  output s0,
  output s1,
  output s2,
  output s3,
  output Co
);

  wire c1, c2, s0_t, s1_t, s2_t, s3_t, s4, s5, s6, s7;

  Multiplexer multiplexer_1 (.sel(Ci), .in_0(s4), .in_1(s0_t), .out(s0));
  CLA_4bit cla_4bit_1 (
    .A0(a0), .B0(b0), .A1(a1), .B1(b1), .A2(a2), .B2(b2), .A3(a3), .B3(b3), .C0(1'b1), .S0(s0_t), .S1(s1_t),
    .S2(s2_t), .S3(s3_t), .C3(c1));
  Multiplexer multiplexer_2 (.sel(Ci), .in_0(s5), .in_1(s1_t), .out(s1));
  Multiplexer multiplexer_3 (.sel(Ci), .in_0(s6), .in_1(s2_t), .out(s2));
  Multiplexer multiplexer_4 (.sel(Ci), .in_0(s7), .in_1(s3_t), .out(s3));
  CLA_4bit cla_4bit_2 (
    .A0(a0), .B0(b0), .A1(a1), .B1(b1), .A2(a2), .B2(b2), .A3(a3), .B3(b3), .C0(1'b0), .S0(s4), .S1(s5),
    .S2(s6), .S3(s7), .C3(c2));
  Multiplexer multiplexer_5 (.sel(Ci), .in_0(c2), .in_1(c1), .out(Co));
endmodule
