// Digital circuit IP.dig as structural Verilog
module IP (
  input  [15:0] cte,
  input  clk,
  input  [2:0] ULA,
  input  Mux_Ip,
  input  Zero,
  output [23:0] IP
);

  wire and_1_out, and_2_out, nand_1_out, or_1_out;
  wire [23:0] bitextender_1_out, multiplexer_1_out, Soma_1_s;

  and and_1 (and_1_out, Mux_Ip, Zero, ULA[0]);
  and and_2 (and_2_out, Mux_Ip, ~ULA[0]);  // And
  or or_1 (or_1_out, and_1_out, and_2_out);
  Multiplexer #(.Bits(24)) multiplexer_1 (
    .sel(or_1_out), .in_0(24'h1), .in_1(bitextender_1_out), .out(multiplexer_1_out));
  BitExtender #(.inputBits(16), .outputBits(24)) bitextender_1 (.in(cte), .out(bitextender_1_out));
  Register #(.Bits(24)) register_1 (.D(Soma_1_s), .C(clk), .en(nand_1_out), .Q(IP));
  // Probe IP on IP
  nand nand_1 (nand_1_out, Mux_Ip, ULA[1]);
  Add #(.Bits(24)) Soma_1 (.a(multiplexer_1_out), .b(IP), .c_i(1'b0), .s(Soma_1_s));  // open: c_o

  // Other names for the same wires on the sheet: Sel__Op__ULA[2:0] = ULA
endmodule
