// Digital circuit inverteSinal.dig as structural Verilog
module inverteSinal (
  input  [31:0] In,
  output [31:0] Out
);

  wire [31:0] not_1_out;

  assign not_1_out = ~In;  // Not not_1, 32 bits wide
  CS_CLA_32bit_adder cs_cla_32bit_adder_1 (.A(not_1_out), .B(32'h1), .S(Out));
endmodule
