// Digital circuit main.dig as structural Verilog
module main (
  input  CLOCK
);

  wire Enable_Display, Mux_Ip, Sel, we, Zero;
  wire [2:0] Sel__Op__ULA;
  wire [3:0] \Memória_de_instrução_d_2 , \Memória_de_instrução_d_3 ;
  wire [15:0] cte;
  wire [23:0] ip_1_ip;
  wire [31:0] Banco_de_Registradores_db, bitextender_1_out, Display, multiplexer_1_out, undriven;
  wire [31:16] \Memória_de_instrução_d ;

  IP ip_1 (.cte(cte), .clk(CLOCK), .ULA(Sel__Op__ULA), .Mux_Ip(Mux_Ip), .Zero(Zero), .IP(ip_1_ip));
  ROM #(.AddrBits(24), .isProgramMemory("true"), .Bits(32)) \Memória_de_instrução  (
    .A(ip_1_ip), .sel(1'b1),
    .D({\Memória_de_instrução_d [31:28], \Memória_de_instrução_d_3 , \Memória_de_instrução_d_2 , \Memória_de_instrução_d [19:16], cte}));
  ROM #(.AddrBits(4), .isProgramMemory("true"), .Bits(7)) \Memória_de_Controle  (
    .A(\Memória_de_instrução_d [31:28]), .sel(1'b1), .D({Sel, Sel__Op__ULA, we, Enable_Display, Mux_Ip}));
  RegisterFile #(.AddrBits(4), .Bits(32)) Banco_de_Registradores (
    .Din(undriven), .we(we), .Rw(\Memória_de_instrução_d [19:16]), .C(CLOCK),
    .Ra(\Memória_de_instrução_d_3 ), .Rb(\Memória_de_instrução_d_2 ), .Da(Display),
    .Db(Banco_de_Registradores_db));
  BitExtender #(.inputBits(16), .outputBits(32)) bitextender_1 (.in(cte), .out(bitextender_1_out));
  Multiplexer #(.Bits(32)) multiplexer_1 (
    .sel(Sel), .in_0(Banco_de_Registradores_db), .in_1(bitextender_1_out), .out(multiplexer_1_out));
  // Probe Display on Display
  ALU alu_1 ();

  // Other names for the same wires on the sheet: clk = CLOCK

  // Notes on the sheet:
  //   contents of Memória_de_instrução (hex, n*v repeats v):
  //   0,b0010001,b0020001,b0030005,e2300003,12120000,d000fffe,f0000000
  //   ,5*0,f0000000
  //   contents of Memória_de_Controle (hex, n*v repeats v):
  //   0,4,c,14,1c,24,2c,34,3c,5c,64,44,2,1,9,11
endmodule
